# Fritzing sketch Arduino_Uno_and_4Relay_Module (saved by Fritzing 0.9.3b)

parts:
  4_Channel_Relay1 = 4 Channel Power Relay
  Part1 = Arduino Uno (Rev3)

nets:
  GND: 4_Channel_Relay1.GND, Part1.GND
  N1: 4_Channel_Relay1.IN1, Part1.D5_PWM
  N2: 4_Channel_Relay1.IN2, Part1.D4
  N3: 4_Channel_Relay1.IN3, Part1.D3_PWM
  N4: 4_Channel_Relay1.IN4, Part1.D2
  VCC: 4_Channel_Relay1.VCC, Part1.5V

custom parts:
  4 Channel Power Relay: A 4 channel power relay. The module operates at 5V.
